# Fritzing sketch fritzingdiagram (saved by Fritzing 0.9.7b)

parts:
  Part1 = Adafruit Motor/Stepper/Servo Shield [part_number="Adafruit #1438"]
  Part2 = Arduino Mega ADK (Rev3)
  Part3 = IR Receiver Breakout [package=PCB]
  M1 = gear-motor
  M2 = gear-motor
  M3 = gear-motor
  M4 = gear-motor
  VCC1 = 4 x AAA Battery Mount

nets:
  N1: Part1.M2A, M1.pin_1
  N2: Part1.M2B, M1.pin_2
  N3: Part1.M1B, M4.pin_1
  N4: Part1.M1A, M4.pin_2
  N5: Part1.M3A, M2.pin_2
  N6: Part1.M3B, M2.pin_1
  N7: Part1.M4B, M3.pin_2
  N8: Part1.M4A, M3.pin_1
  N9: Part1.GND, VCC1.-
  N10: Part1.VMOTOR, VCC1.+
  N11: Part2.D19/RX1, Part3.OUT
  5V: Part2.5V, Part3.VCC
  GND: Part2.GND, Part3.GND

notes:
  FLYSKY Receiver
  I-BUS Pin goes to Pin 19 on Arduino

custom parts:
  Adafruit Motor/Stepper/Servo Shield: The original Adafruit Motorshield kit is one of our most beloved kits, which is why we decided to make something even better. We have upgraded the shield kit to make the bestest, easiest way to drive DC and Stepper motors. This shield will make quick work of your next robotics project! We kept the ability to drive up to 4 DC motors or 2 stepper motors, but added many improvements: Instead of a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
